# Fritzing sketch c64_gpio_connector (saved by Fritzing 0.9.0b)
circuit board: 8.46667cm x 5.64444cm
breadboards: 1

parts:
  Pi1 = Adafruit Pi Cobbler
  C64connector = male pin header, 20 pins [form="♂ (male)"]

nets:
  N1: Pi1.3V3, C64connector.pin3
  N2: Pi1.SDA0, C64connector.pin20
  N3: Pi1.SCL0, C64connector.pin19
  N4: Pi1.#4, C64connector.pin18
  N5: Pi1.TXD, C64connector.pin1
  N6: Pi1.RXD, C64connector.pin5
  N7: Pi1.#17, C64connector.pin17
  N8: Pi1.#18, C64connector.pin6
  N9: Pi1.#21, C64connector.pin16
  N10: Pi1.#22, C64connector.pin15
  N11: Pi1.#23, C64connector.pin7
  N12: Pi1.#24, C64connector.pin8
  N13: Pi1.MOSI, C64connector.pin14
  N14: Pi1.MISO, C64connector.pin13
  N15: Pi1.#25, C64connector.pin9
  N16: Pi1.SCLK, C64connector.pin12
  N17: Pi1.CE0, C64connector.pin10
  N18: Pi1.CE1, C64connector.pin11

custom parts:
  Adafruit Pi Cobbler: Adafruit Pi Cobbler GPIO Breakout for Raspberry Pi
